// Logisim project pong_cpu.circ as structural Verilog
module FullAdder (
  input  A,
  input  B,
  input  Cin,
  output SUM,
  output COUT
);

  wire and_1_out, and_2_out, xor_1_out;

  xor xor_1 (xor_1_out, A, B);
  and and_1 (and_1_out, B, A);
  xor xor_2 (SUM, xor_1_out, Cin);
  and and_2 (and_2_out, Cin, xor_1_out);
  or or_1 (COUT, and_2_out, and_1_out);
endmodule

module FourBitAdder (
  input  B3,
  input  A3,
  input  A2,
  input  B1,
  input  A1,
  input  B2,
  input  B0,
  input  A0,
  input  C0,
  output Cin_3_ou,
  output S0,
  output S2,
  output S1,
  output COUT,
  output S3
);

  wire fulladder_2_cout, fulladder_3_cout, fulladder_4_cout;

  FullAdder fulladder_1 (.A(A3), .B(B3), .Cin(fulladder_2_cout), .SUM(S3), .COUT(COUT));
  FullAdder fulladder_2 (.A(A2), .B(B2), .Cin(fulladder_3_cout), .SUM(S2), .COUT(fulladder_2_cout));
  FullAdder fulladder_3 (.A(A1), .B(B1), .Cin(fulladder_4_cout), .SUM(S1), .COUT(fulladder_3_cout));
  FullAdder fulladder_4 (.A(A0), .B(B0), .Cin(C0), .SUM(S0), .COUT(fulladder_4_cout));
endmodule

module AND4 (
  input  [3:0] A,
  input  [3:0] B,
  output [3:0] R
);

  assign R = A & B;  // AND_Gate and_1, 4 bits wide
endmodule

module OR4 (
  input  [3:0] A,
  input  [3:0] B,
  output [3:0] R
);

  assign R = A | B;  // OR_Gate or_1, 4 bits wide
endmodule

module XOR4 (
  input  [3:0] A,
  input  [3:0] B,
  output [3:0] R
);

  assign R = A ^ B;  // XOR_Gate xor_1, 4 bits wide
endmodule

module ArithmeticUnit (
  input  [3:0] B,
  input  [3:0] A,
  input  SUB,
  output Cin_3_ou,
  output [3:0] AUResult,
  output COUT
);

  wire [3:0] bit_extender_1_out, xor4_1_r;

  assign bit_extender_1_out = {{3{SUB}}, SUB};  // Bit_Extender bit_extender_1
  XOR4 xor4_1 (.A(bit_extender_1_out), .B(B), .R(xor4_1_r));
  FourBitAdder fourbitadder_1 (
    .B3(xor4_1_r[3]), .A3(A[3]), .A2(A[2]), .B1(xor4_1_r[1]), .A1(A[1]), .B2(xor4_1_r[2]), .B0(xor4_1_r[0]),
    .A0(A[0]), .C0(SUB), .Cin_3_ou(Cin_3_ou), .S0(AUResult[0]), .S2(AUResult[2]), .S1(AUResult[1]),
    .COUT(COUT), .S3(AUResult[3]));
endmodule

module ALU (
  input  [3:0] A,
  input  [3:0] B,
  input  [2:0] OPRATION,
  output Cin_3_ou,
  output AluCout,
  output [3:0] AluResult
);

  wire [3:0] arithmeticunit_1_auresult, lu_1_and_res, lu_1_or_res, lu_1_xor_res;

  ArithmeticUnit arithmeticunit_1 (
    .B(B), .A(A), .SUB(OPRATION[0]), .Cin_3_ou(Cin_3_ou), .AUResult(arithmeticunit_1_auresult), .COUT(AluCout));
  LU lu_1 (.A(A), .B(B), .AND_RES(lu_1_and_res), .OR_RES(lu_1_or_res), .XOR_RES(lu_1_xor_res));
  Multiplexer #(.select(3), .width(4)) multiplexer_1 (
    .in0(arithmeticunit_1_auresult), .in1(arithmeticunit_1_auresult), .in2(lu_1_and_res), .in3(lu_1_or_res),
    .in4(lu_1_xor_res), .out(AluResult), .sel(OPRATION));  // open: in5, in6, in7
endmodule

module LU (
  input  [3:0] A,
  input  [3:0] B,
  output [3:0] AND_RES,
  output [3:0] OR_RES,
  output [3:0] XOR_RES
);

  AND4 and4_1 (.A(A), .B(B), .R(AND_RES));
  OR4 or4_1 (.A(A), .B(B), .R(OR_RES));
  XOR4 xor4_1 (.A(A), .B(B), .R(XOR_RES));
endmodule

module SRLatch (
  input  R,
  input  S,
  output Q,
  output NotQ
);

  nor nor_1 (Q, R, NotQ);
  nor nor_2 (NotQ, Q, S);
endmodule

module DLatchEN (
  input  D,
  input  EN,
  output Q,
  output NotQ
);

  wire and_1_out, and_2_out, not_1_out;

  not not_1 (not_1_out, D);
  and and_1 (and_1_out, D, EN);
  and and_2 (and_2_out, EN, not_1_out);
  SRLatch srlatch_1 (.R(and_2_out), .S(and_1_out), .Q(Q), .NotQ(NotQ));
endmodule

module DFlipFlop (
  input  D,
  input  CLOCK,
  output Q,
  output NotQ
);

  wire Master_q, not_1_out;

  not not_1 (not_1_out, CLOCK);
  DLatchEN Master (.D(D), .EN(not_1_out), .Q(Master_q));  // open: NotQ
  DLatchEN Slave (.D(Master_q), .EN(CLOCK), .Q(Q), .NotQ(NotQ));
endmodule

module FourBitRegister (
  input  LOAD,
  input  CLOCK,
  input  D3,
  input  D2,
  input  D1,
  input  D0,
  output Q3,
  output Q2,
  output Q1,
  output Q0
);

  wire multiplexer_1_out, multiplexer_2_out, multiplexer_3_out, multiplexer_4_out;

  Multiplexer multiplexer_1 (.in0(Q3), .in1(D3), .out(multiplexer_1_out), .sel(LOAD));
  Multiplexer multiplexer_2 (.in0(Q2), .in1(D2), .out(multiplexer_2_out), .sel(LOAD));
  Multiplexer multiplexer_3 (.in0(Q1), .in1(D1), .out(multiplexer_3_out), .sel(LOAD));
  Multiplexer multiplexer_4 (.in0(Q0), .in1(D0), .out(multiplexer_4_out), .sel(LOAD));
  DFlipFlop DFF3 (.D(multiplexer_1_out), .CLOCK(CLOCK), .Q(Q3));  // open: NotQ
  DFlipFlop DFF2 (.D(multiplexer_2_out), .CLOCK(CLOCK), .Q(Q2));  // open: NotQ
  DFlipFlop DFF1 (.D(multiplexer_3_out), .CLOCK(CLOCK), .Q(Q1));  // open: NotQ
  DFlipFlop DFF0 (.D(multiplexer_4_out), .CLOCK(CLOCK), .Q(Q0));  // open: NotQ
endmodule

module Decoder2to4 (
  input  A1,
  input  A0,
  output Y0,
  output Y1,
  output Y2,
  output Y3
);

  wire not_1_out, not_2_out;

  not not_1 (not_1_out, A0);
  not not_2 (not_2_out, A1);
  and and_1 (Y0, not_1_out, not_2_out);
  and and_2 (Y1, not_2_out, A0);
  and and_3 (Y2, not_1_out, A1);
  and and_4 (Y3, A0, A1);
endmodule

module RegisterFile (
  input  D3,
  input  D2,
  input  D1,
  input  D0,
  input  CLOCK,
  input  [1:0] READ_ADRS_A,
  input  [1:0] READ_ADRS_B,
  input  Decoder_A0,
  input  Decoder_A1,
  output [3:0] READ_A,
  output [3:0] READ_B
);

  wire decoder2to4_1_y0, decoder2to4_1_y1, decoder2to4_1_y2, decoder2to4_1_y3;
  wire [3:0] R0_q0, R1_q0, R2_q0, R3_q0;

  FourBitRegister R0 (
    .LOAD(decoder2to4_1_y0), .CLOCK(CLOCK), .D3(D3), .D2(D2), .D1(D1), .D0(D0), .Q3(R0_q0[3]), .Q2(R0_q0[2]),
    .Q1(R0_q0[1]), .Q0(R0_q0[0]));
  FourBitRegister R1 (
    .LOAD(decoder2to4_1_y1), .CLOCK(CLOCK), .D3(D3), .D2(D2), .D1(D1), .D0(D0), .Q3(R1_q0[3]), .Q2(R1_q0[2]),
    .Q1(R1_q0[1]), .Q0(R1_q0[0]));
  FourBitRegister R2 (
    .LOAD(decoder2to4_1_y2), .CLOCK(CLOCK), .D3(D3), .D2(D2), .D1(D1), .D0(D0), .Q3(R2_q0[3]), .Q2(R2_q0[2]),
    .Q1(R2_q0[1]), .Q0(R2_q0[0]));
  FourBitRegister R3 (
    .LOAD(decoder2to4_1_y3), .CLOCK(CLOCK), .D3(D3), .D2(D2), .D1(D1), .D0(D0), .Q3(R3_q0[3]), .Q2(R3_q0[2]),
    .Q1(R3_q0[1]), .Q0(R3_q0[0]));
  Decoder2to4 decoder2to4_1 (
    .A1(Decoder_A0), .A0(Decoder_A1), .Y0(decoder2to4_1_y0), .Y1(decoder2to4_1_y1), .Y2(decoder2to4_1_y2),
    .Y3(decoder2to4_1_y3));
  Multiplexer #(.select(2), .width(4)) multiplexer_1 (
    .in0(R0_q0), .in1(R1_q0), .in2(R2_q0), .in3(R3_q0), .out(READ_A), .sel(READ_ADRS_A));
  Multiplexer #(.select(2), .width(4)) multiplexer_2 (
    .in0(R0_q0), .in1(R1_q0), .in2(R2_q0), .in3(R3_q0), .out(READ_B), .sel(READ_ADRS_B));
endmodule

module Datapath (
  input  ACC_LOAD,
  input  ACC_SELECTOR,
  input  [1:0] ACC_IN_SEL,
  input  Toggle,
  input  [2:0] ALU_OPCODE,
  input  [3:0] Memory,
  input  [1:0] ADRESS_WRITE_TO,
  input  IR_LOAD,
  output Cin_3_ou,
  output Cout
);

  wire clock_1_out;
  wire [1:0] instructionregister_1_ir_operand;
  wire [3:0] accumulator_1_acc, alu_1_aluresult, instructionregister_1_ir_opcode, multiplexer_1_out,
       multiplexer_2_out, multiplexer_3_out, registerfile_1_read_a, registerfile_1_read_b;
  wire [3:2] instructionregister_1_ir_operand_2;

  Multiplexer #(.select(2), .width(4)) multiplexer_1 (
    .in0(alu_1_aluresult), .in1(registerfile_1_read_a),
    .in2({instructionregister_1_ir_operand_2, instructionregister_1_ir_operand}), .out(multiplexer_1_out),
    .sel(ACC_IN_SEL));  // open: in3
  Clock clock_1 (.out(clock_1_out));
  Accumulator accumulator_1 (.LOAD(ACC_LOAD), .CLK(clock_1_out), .DATA_IN(multiplexer_1_out), .ACC(accumulator_1_acc));
  RegisterFile registerfile_1 (
    .D3(multiplexer_3_out[3]), .D2(multiplexer_3_out[2]), .D1(multiplexer_3_out[1]),
    .D0(multiplexer_3_out[0]), .CLOCK(clock_1_out), .READ_ADRS_A(instructionregister_1_ir_operand),
    .READ_ADRS_B(instructionregister_1_ir_operand), .Decoder_A0(ADRESS_WRITE_TO[0]),
    .Decoder_A1(ADRESS_WRITE_TO[1]), .READ_A(registerfile_1_read_a), .READ_B(registerfile_1_read_b));
  Multiplexer #(.width(4)) multiplexer_2 (
    .in0(registerfile_1_read_a), .in1(accumulator_1_acc), .out(multiplexer_2_out), .sel(ACC_SELECTOR));
  InstructionRegister instructionregister_1 (
    .CLK(clock_1_out), .LOAD(IR_LOAD),
    .IR_OPERAND({instructionregister_1_ir_operand_2, instructionregister_1_ir_operand}),
    .IR_OPCODE(instructionregister_1_ir_opcode));  // open: INSTRUCTION
  ALU alu_1 (
    .A(multiplexer_2_out), .B(registerfile_1_read_b), .OPRATION(ALU_OPCODE), .Cin_3_ou(Cin_3_ou),
    .AluCout(Cout), .AluResult(alu_1_aluresult));
  Multiplexer #(.width(4)) multiplexer_3 (.in0(alu_1_aluresult), .in1(Memory), .out(multiplexer_3_out), .sel(Toggle));
endmodule

module Flags (
  input  ALU_COUT,
  input  [3:0] ALU_Res,
  input  Cin_3_ou,
  output C,
  output Z,
  output N,
  output V
);

  wire or_1_out, or_2_out, or_3_out;

  or or_1 (or_1_out, ALU_Res[2], ALU_Res[3]);
  or or_2 (or_2_out, ALU_Res[1], or_1_out);
  xor xor_1 (V, Cin_3_ou, ALU_COUT);
  or or_3 (or_3_out, ALU_Res[0], or_2_out);
  not not_1 (Z, or_3_out);

  assign C = ALU_COUT;
  assign N = ALU_Res[3];
endmodule

module ProgramCounter (
  input  LOAD_REG,
  input  CLK,
  input  [3:0] CONST_0001,
  input  [2:0] ADD_OP,
  input  [3:0] in_5,
  input  [3:0] LOAD_VALUE,
  input  RESET,
  input  LOAD,
  output [3:0] PC
);

  wire [3:0] alu_1_aluresult, multiplexer_1_out, multiplexer_2_out;

  ALU alu_1 (.A(PC), .B(CONST_0001), .OPRATION(ADD_OP), .AluResult(alu_1_aluresult));  // open: Cin_3_ou, AluCout
  Multiplexer #(.width(4)) multiplexer_1 (.in0(alu_1_aluresult), .in1(LOAD_VALUE), .out(multiplexer_1_out), .sel(LOAD));
  Multiplexer #(.width(4)) multiplexer_2 (.in0(multiplexer_1_out), .in1(in_5), .out(multiplexer_2_out), .sel(RESET));
  FourBitRegister fourbitregister_1 (
    .LOAD(LOAD_REG), .CLOCK(CLK), .D3(multiplexer_2_out[3]), .D2(multiplexer_2_out[2]),
    .D1(multiplexer_2_out[1]), .D0(multiplexer_2_out[0]), .Q3(PC[3]), .Q2(PC[2]), .Q1(PC[1]), .Q0(PC[0]));
endmodule

module InstructionRegister (
  input  [7:0] INSTRUCTION,
  input  CLK,
  input  LOAD,
  output [3:0] IR_OPERAND,
  output [3:0] IR_OPCODE
);

  FourBitRegister IR0 (
    .LOAD(LOAD), .CLOCK(CLK), .D3(INSTRUCTION[3]), .D2(INSTRUCTION[2]), .D1(INSTRUCTION[1]),
    .D0(INSTRUCTION[0]), .Q3(IR_OPERAND[3]), .Q2(IR_OPERAND[2]), .Q1(IR_OPERAND[1]), .Q0(IR_OPERAND[0]));
  FourBitRegister IR1 (
    .LOAD(LOAD), .CLOCK(CLK), .D3(INSTRUCTION[7]), .D2(INSTRUCTION[6]), .D1(INSTRUCTION[5]),
    .D0(INSTRUCTION[4]), .Q3(IR_OPCODE[3]), .Q2(IR_OPCODE[2]), .Q1(IR_OPCODE[1]), .Q0(IR_OPCODE[0]));
endmodule

module Accumulator (
  input  LOAD,
  input  CLK,
  input  [3:0] DATA_IN,
  output [3:0] ACC
);

  FourBitRegister fourbitregister_1 (
    .LOAD(LOAD), .CLOCK(CLK), .D3(DATA_IN[3]), .D2(DATA_IN[2]), .D1(DATA_IN[1]), .D0(DATA_IN[0]),
    .Q3(ACC[3]), .Q2(ACC[2]), .Q1(ACC[1]), .Q0(ACC[0]));
endmodule

module ControlUnit (
  input  ENABLE,
  input  [3:0] IR_OPCODE,
  output ACC_LOAD
);

  wire decoder_1_out0, decoder_1_out1, decoder_1_out2, decoder_1_out3, decoder_1_out4, decoder_1_out5,
       decoder_1_out6, decoder_1_out7, decoder_1_out8;

  Decoder #(.select(4)) decoder_1 (
    .out0(decoder_1_out0), .out1(decoder_1_out1), .out2(decoder_1_out2), .out3(decoder_1_out3),
    .out4(decoder_1_out4), .out5(decoder_1_out5), .out6(decoder_1_out6), .out7(decoder_1_out7),
    .out8(decoder_1_out8), .sel(IR_OPCODE), .en(ENABLE));  // open: out9, out10, out11, out12, out13, out14, out15
  or or_1 (ACC_LOAD, decoder_1_out0, decoder_1_out1, decoder_1_out2, decoder_1_out3, decoder_1_out4, decoder_1_out5, decoder_1_out6, decoder_1_out7, decoder_1_out8);
endmodule
